# Fritzing sketch LCD_I2C_1602 (saved by Fritzing 0.9.3b)

parts:
  Composant1 = LCD1602-I2C
  Raspberry_Pi_1 = Raspberry Pi 3 [part_number=RPI-3-V1.2]

nets:
  GND: Composant1.GND, Raspberry_Pi_1.GND
  VCC: Composant1.VCC, Raspberry_Pi_1.5V
  N1: Composant1.SDA, Raspberry_Pi_1.GPIO2
  N2: Composant1.SCL, Raspberry_Pi_1.GPIO3

custom parts:
  LCD1602-I2C: A standard character display, usually with 2x16 characters. Comes in many colors with LCM1602 IIC attached.
