# Fritzing sketch Motion_Buzzer (saved by Fritzing 0.9.3b)
breadboards: 1

parts:
  Raspberry_Pi_1 = Raspberry Pi 3 [part_number=RPI-3-V1.2]
  PIR1 = PIR sensor
  J1 = Piezo Speaker

nets:
  N1: Raspberry_Pi_1.GIPO23, PIR1.SIG
  N2: Raspberry_Pi_1.GIPO18, J1.pin2
  GND: Raspberry_Pi_1.GND, PIR1.GND, J1.pin1
  5V: Raspberry_Pi_1.5V, PIR1.VDD
