# Fritzing sketch Push_Button (saved by Fritzing 0.9.3b)
breadboards: 1

parts:
  LED1 = smd LED [color="Red (633nm)" package="0603 [SMD]"]
  R1 = Resistor [tolerance=±5% resistance=600 package="0603 [SMD]"]
  S1 = Pushbutton [package="[SMD]"]
  Raspberry_Pi_1 = Raspberry Pi 3 [part_number=RPI-3-V1.2]

nets:
  N1: LED1.cathode, Raspberry_Pi_1.GPIO3, Raspberry_Pi_1.GND
  N2: LED1.anode, R1.Pin_1
  N3: R1.Pin_0, S1.Pin_1, S1.Pin_2
  N4: S1.Pin_3, S1.Pin_4, Raspberry_Pi_1.GIPO18
