# Fritzing sketch Servo_Motor (saved by Fritzing 0.9.3b)

parts:
  Raspberry_Pi_1 = Raspberry Pi 3 [part_number=RPI-3-V1.2]
  M1 = Dagu DGServo 9g (Top view) [part_number=RS001B]

nets:
  N1: Raspberry_Pi_1.GIPO17, M1.pulse
  GND: Raspberry_Pi_1.GND, M1.gnd
  5V: Raspberry_Pi_1.5V, M1.vcc
