# Fritzing sketch Step_Motor (saved by Fritzing 0.9.3b)

parts:
  Raspberry_Pi_1 = Raspberry Pi 3 [part_number=RPI-3-V1.2]
  X1 = X113647 Stepper Driver Board [package=board]
  MOTOR1 = 28BYJ-48 Stepper Motor  # not connected

nets:
  N1: Raspberry_Pi_1.GIPO4, X1.IN1
  N2: Raspberry_Pi_1.GIPO17, X1.IN2
  N3: Raspberry_Pi_1.GIPO27, X1.IN3
  N4: Raspberry_Pi_1.GIPO22, X1.IN4
  GND: Raspberry_Pi_1.GND, X1.GND
  N5: Raspberry_Pi_1.5V, X1.+V

custom parts:
  X113647 Stepper Driver Board: A common stepper motor driver board based on ULN2003APG darlington array
  28BYJ-48 Stepper Motor: 28BYJ-48 gear-reduction stepper motor (small)
